# Fritzing sketch sensorGas (saved by Fritzing 0.9.1b)
breadboards: 1

parts:
  U1 = GAS_SENSOR [package=mq-3]
  Parte1 = Arduino Uno (Rev3)

nets:
  N1: U1.B1, Parte1.GND
  N2: U1.A1, Parte1.5V
  N3: U1.H1, Parte1.A1

notes:
  Este esquema es para el sensor MQ5
  En el cual se ocupan 3 pines, GND, VCC y OUT
  los cuales estan descritos
