# Fritzing sketch SensorMovimiento (saved by Fritzing 0.9.1b)
breadboards: 1

parts:
  Parte1 = Arduino Uno (Rev3) - ICSP
  PIR1 = PIR sensor

nets:
  N1: Parte1.D2, PIR1.SIG
  5V: Parte1.5V, PIR1.VDD
  GND: Parte1.GND, PIR1.GND
